// Logisim project Lab3.circ as structural Verilog: 1 circuit, main circuit main
module main (
  input  X,
  input  y,
  input  z,
  output E_x_y_z
);

  wire and_1_out, and_2_out, and_3_out, and_4_out, not_1_out, not_2_out, not_3_out;

  not not_1 (not_1_out, y);
  not not_2 (not_2_out, z);
  not not_3 (not_3_out, X);
  and and_1 (and_1_out, not_3_out, y);
  and and_2 (and_2_out, not_3_out, z);
  and and_3 (and_3_out, y, z);
  and and_4 (and_4_out, X, not_1_out, not_2_out);
  or or_1 (E_x_y_z, and_1_out, and_2_out, and_3_out, and_4_out);
endmodule
